// Logisim project contadorHoras.circ as structural Verilog: 1 circuit, main circuit contadorHoras(00-23)
module contadorHoras_00_23 (
  input  CLK,
  input  EN,
  output T1,
  output T0,
  output U3,
  output U2,
  output U1,
  output U0
);

  wire a7, A9, ab, b8, C10, DT0, DT1, DU0, DU1, DU2, DU3, e1, e2, ENn, fT0, fT1, fU0, fU1, fU2, fU3, H, K2,
       K3, K4, K5, M, mAT0, mAT1, mAU0, mAU1, mAU2, mAU3, mBT0, mBT1, mBU0, mBU1, mBU2, mBU3, N1, nT0, nT1,
       nU0, nU1, nU2, nU3, P1, P2, P3, P4, S, t1_t, t2, t3, X, Y, Z21, Z210, ZM, Zz;

  not not_1 (nT1, T1);
  not not_2 (nT0, T0);
  not not_3 (nU3, U3);
  not not_4 (nU2, U2);
  not not_5 (nU1, U1);
  not not_6 (nU0, U0);
  not not_7 (ENn, EN);
  and and_1 (C10, U1, U0);
  nand nand_1 (M, U1, U0);
  and and_2 (Z21, nU2, nU1);
  and and_3 (Zz, nU3, nU2);
  and and_4 (mBT1, ENn, T1);
  and and_5 (mBT0, ENn, T0);
  and and_6 (a7, nU3, U2, C10);
  and and_7 (mBU3, ENn, U3);
  and and_8 (H, nT1, nU3);
  and and_9 (mBU2, ENn, U2);
  and and_10 (e1, nU1, U0);
  and and_11 (e2, U1, nU0);
  and and_12 (N1, nT0, nU2);
  and and_13 (mBU1, ENn, U1);
  and and_14 (mBU0, ENn, U0);
  and and_15 (A9, U3, Z21, U0);
  and and_16 (Z210, Z21, nU0);
  and and_17 (ZM, Zz, M);
  and and_18 (t1_t, H, U2, nU1);
  and and_19 (t2, H, U2, nU0);
  and and_20 (t3, H, nU2, C10);
  or or_1 (Y, e1, e2);
  or or_2 (X, nT1, N1);
  or or_3 (K2, nU3, Z21);
  and and_21 (K4, T1, nT0, Zz);
  and and_22 (P1, nT1, T0, A9);
  and and_23 (P2, T1, nT0, ZM);
  and and_24 (P3, nT1, nT0, A9);
  or or_4 (S, nU3, Z210);
  and and_25 (b8, U3, Z210);
  or or_5 (fU2, t1_t, t2, t3);
  and and_26 (fU1, nU3, X, Y);
  and and_27 (K3, nT1, K2);
  or or_6 (fT1, P1, P2);
  and and_28 (P4, nT1, T0, S);
  or or_7 (ab, a7, b8);
  and and_29 (mAU2, EN, fU2);
  and and_30 (mAU1, EN, fU1);
  or or_8 (K5, K3, K4);
  and and_31 (mAT1, EN, fT1);
  or or_9 (fT0, P3, P4);
  and and_32 (fU3, nT1, ab);
  or or_10 (DU2, mAU2, mBU2);
  or or_11 (DU1, mAU1, mBU1);
  and and_33 (fU0, nU0, K5);
  or or_12 (DT1, mAT1, mBT1);
  and and_34 (mAT0, EN, fT0);
  and and_35 (mAU3, EN, fU3);
  and and_36 (mAU0, EN, fU0);
  or or_13 (DT0, mAT0, mBT0);
  or or_14 (DU3, mAU3, mBU3);
  or or_15 (DU0, mAU0, mBU0);
  D_Flip_Flop FF_T1 (.clk(CLK), .D(DT1), .Q(T1));  // open: Qn, preset, en, reset
  D_Flip_Flop FF_T0 (.clk(CLK), .D(DT0), .Q(T0));  // open: Qn, preset, en, reset
  D_Flip_Flop FF_U3 (.clk(CLK), .D(DU3), .Q(U3));  // open: Qn, preset, en, reset
  D_Flip_Flop FF_U2 (.clk(CLK), .D(DU2), .Q(U2));  // open: Qn, preset, en, reset
  D_Flip_Flop FF_U1 (.clk(CLK), .D(DU1), .Q(U1));  // open: Qn, preset, en, reset
  D_Flip_Flop FF_U0 (.clk(CLK), .D(DU0), .Q(U0));  // open: Qn, preset, en, reset

  // Notes on the sheet:
  //   Termos compartilhados (literais invertidos, EN invertido, decodificacoes comuns)
  //   Logica de DT1 (f -> mux de enable -> flip-flop)
  //   Logica de DT0 (f -> mux de enable -> flip-flop)
  //   Logica de DU3 (f -> mux de enable -> flip-flop)
  //   Logica de DU2 (f -> mux de enable -> flip-flop)
  //   Logica de DU1 (f -> mux de enable -> flip-flop)
  //   Logica de DU0 (f -> mux de enable -> flip-flop)
  //   Contador de horas 00-23 (BCD): T1T0 = dezena da hora, U3U2U1U0 = unidade da hora
  //   CLK = clock (mesmo dos outros contadores) | EN = habilita a contagem (ligar no CO da dezena de minuto)
  //   Todos os D passam pelo mux D = EN*f + EN'*Q. Estados invalidos voltam para 00.
endmodule
