// Logisim project contadorUnidades.circ as structural Verilog: 3 circuits, main circuit main
module main (
);

  contadorDezenas_0_5__circ contadordezenas_0_5_circ_1 ();  // open: CLK, EN
endmodule

module contadorUnidades_0_9__circ (
  input  CLK,
  input  EN
);

  wire and_1_out, and_2_out, and_3_out, and_4_out, and_5_out, and_6_out, and_7_out, and_8_out, and_9_out,
       and_10_out, and_11_out, and_12_out, and_13_out, and_14_out, and_15_out, and_16_out, D0_q, D1_q, D2_q,
       D3_q, nand_1_out, not_1_out, not_2_out, not_3_out, not_4_out, not_5_out, not_6_out, not_7_out,
       not_8_out, not_9_out, not_10_out, not_11_out, not_12_out, or_1_out, or_2_out, or_3_out, or_4_out,
       or_5_out, or_6_out, or_7_out, xor_1_out;

  not not_1 (not_1_out, D2_q);
  not not_2 (not_2_out, D0_q);
  not not_3 (not_3_out, D3_q);
  not not_4 (not_4_out, D1_q);
  and and_1 (and_1_out, D3_q, not_1_out, not_4_out, not_2_out);
  and and_2 (and_2_out, not_3_out, D2_q, D1_q, D0_q);
  or or_1 (or_1_out, and_1_out, and_2_out);
  not not_5 (not_5_out, EN);
  D_Flip_Flop D3 (.clk(CLK), .D(or_2_out), .Q(D3_q));  // open: Qn, preset, en, reset
  not not_6 (not_6_out, D3_q);
  and and_3 (and_3_out, or_1_out, EN);
  or or_2 (or_2_out, and_3_out, and_4_out);
  and and_4 (and_4_out, D3_q, not_5_out);
  D_Flip_Flop D2 (.clk(CLK), .D(or_4_out), .Q(D2_q));  // open: Qn, preset, en, reset
  not not_7 (not_7_out, D2_q);
  nand nand_1 (nand_1_out, D1_q, D0_q);
  and and_5 (and_5_out, D2_q, nand_1_out);
  or or_3 (or_3_out, and_5_out, and_9_out);
  and and_6 (and_6_out, not_6_out, or_3_out);
  and and_7 (and_7_out, and_6_out, EN);
  and and_8 (and_8_out, D2_q, not_5_out);
  xor xor_1 (xor_1_out, D1_q, D0_q);
  and and_9 (and_9_out, not_7_out, D1_q, D0_q);
  or or_4 (or_4_out, and_7_out, and_8_out);
  D_Flip_Flop D1 (.clk(CLK), .D(or_5_out), .Q(D1_q));  // open: Qn, preset, en, reset
  not not_8 (not_8_out, D3_q);
  and and_10 (and_10_out, xor_1_out, not_8_out);
  and and_11 (and_11_out, and_10_out, EN);
  or or_5 (or_5_out, and_11_out, and_12_out);
  and and_12 (and_12_out, D1_q, not_5_out);
  D_Flip_Flop D0 (.clk(CLK), .D(or_7_out), .Q(D0_q));  // open: Qn, preset, en, reset
  not not_9 (not_9_out, D2_q);
  not not_10 (not_10_out, D1_q);
  and and_13 (and_13_out, not_9_out, not_10_out);
  not not_11 (not_11_out, D3_q);
  or or_6 (or_6_out, not_11_out, and_13_out);
  not not_12 (not_12_out, D0_q);
  and and_14 (and_14_out, or_6_out, not_12_out);
  and and_15 (and_15_out, and_14_out, EN);
  and and_16 (and_16_out, D0_q, not_5_out);
  or or_7 (or_7_out, and_15_out, and_16_out);
  main main_1 ();
endmodule

module contadorDezenas_0_5__circ (
  input  CLK,
  input  EN
);

  wire and_1_out, and_2_out, and_3_out, and_4_out, and_5_out, and_6_out, and_7_out, and_8_out, and_9_out,
       and_10_out, D0_q, D1_q, D2_q, not_1_out, not_2_out, not_3_out, not_4_out, not_5_out, not_6_out,
       not_7_out, not_8_out, or_1_out, or_2_out, or_3_out, or_4_out, or_5_out, xor_1_out;

  not not_1 (not_1_out, D2_q);
  not not_2 (not_2_out, EN);
  D_Flip_Flop D2 (.clk(CLK), .D(or_2_out), .Q(D2_q));  // open: Qn, preset, en, reset
  and and_1 (and_1_out, not_1_out, D1_q, D0_q);
  or or_1 (or_1_out, and_1_out, and_2_out);
  not not_3 (not_3_out, D0_q);
  not not_4 (not_4_out, D1_q);
  and and_2 (and_2_out, D2_q, not_4_out, not_3_out);
  and and_3 (and_3_out, or_1_out, EN);
  and and_4 (and_4_out, D2_q, not_2_out);
  D_Flip_Flop D1 (.clk(CLK), .D(or_4_out), .Q(D1_q));  // open: Qn, preset, en, reset
  not not_5 (not_5_out, D2_q);
  and and_5 (and_5_out, not_5_out, xor_1_out);
  or or_2 (or_2_out, and_3_out, and_4_out);
  not not_6 (not_6_out, D2_q);
  xor xor_1 (xor_1_out, D1_q, D0_q);
  or or_3 (or_3_out, not_6_out, not_7_out);
  and and_6 (and_6_out, and_5_out, EN);
  and and_7 (and_7_out, D1_q, not_2_out);
  D_Flip_Flop D0 (.clk(CLK), .D(or_5_out), .Q(D0_q));  // open: Qn, preset, en, reset
  not not_7 (not_7_out, D1_q);
  not not_8 (not_8_out, D0_q);
  and and_8 (and_8_out, or_3_out, not_8_out);
  and and_9 (and_9_out, and_8_out, EN);
  and and_10 (and_10_out, D0_q, not_2_out);
  or or_4 (or_4_out, and_6_out, and_7_out);
  or or_5 (or_5_out, and_9_out, and_10_out);
endmodule
