// Logisim project decodificador7seg.circ as structural Verilog: 1 circuit, main circuit decodificadorBCD-7seg
module decodificadorBCD_7seg (
  input  I3,
  input  I2,
  input  I1,
  input  I0,
  output a,
  output b,
  output c,
  output d,
  output e,
  output f,
  output g
);

  wire a1, d1, d2, f1, g1, I1I0, I1nI0, I2I0, I2nI0, I2nI1, I2nI1I0, nI0, nI1, nI1nI0, nI2, nI2I1, nI2nI0;

  not not_1 (nI2, I2);
  not not_2 (nI1, I1);
  not not_3 (nI0, I0);
  and and_1 (I2I0, I2, I0);
  and and_2 (I1I0, I1, I0);
  and and_3 (nI2nI0, nI2, nI0);
  and and_4 (nI1nI0, nI1, nI0);
  and and_5 (nI2I1, nI2, I1);
  and and_6 (I1nI0, I1, nI0);
  and and_7 (I2nI1, I2, nI1);
  and and_8 (I2nI0, I2, nI0);
  or or_1 (a1, I3, I2I0);
  or or_2 (c, nI1, I2, I0);
  and and_9 (I2nI1I0, I2, nI1, I0);
  or or_3 (a, a1, nI2nI0, I1);
  or or_4 (b, nI1nI0, nI2, I1I0);
  or or_5 (d1, nI2I1, nI2nI0);
  or or_6 (e, nI2nI0, I1nI0);
  or or_7 (f1, I2nI1, I2nI0);
  or or_8 (g1, I2nI0, nI2I1);
  or or_9 (d2, d1, I1nI0);
  or or_10 (f, f1, nI1nI0, I3);
  or or_11 (g, g1, I2nI1, I3);
  or or_12 (d, d2, I2nI1I0, I3);
  _7_Segment_Display u_7_segment_display_1 (.g(g), .f(f), .a(a), .b(b), .e(e), .d(d), .c(c));  // open: dp

  // Notes on the sheet:
  //   Termos compartilhados (complementos e produtos usados por mais de um segmento)
  //   Segmento a
  //   Segmento b
  //   Segmento c
  //   Segmento d
  //   Segmento e
  //   Segmento f
  //   Segmento g
  //   Decodificador BCD -> 7 segmentos (ativo em 1): I3 I2 I1 I0 = digito BCD (I3 = bit mais significativo)
  //   Saidas: a=topo b=sup.direita c=inf.direita d=base e=inf.esquerda f=sup.esquerda g=meio
  //   Entradas 10 a 15 nao ocorrem (don't care).
  //   Display de teste (pode apagar)
endmodule
