// Logisim project projetoQuase.circ as structural Verilog
module decodificadorA (
  input  B4,
  input  B3,
  input  B2,
  input  B1,
  output out_5
);

  wire xnor_1_out;

  xnor xnor_1 (xnor_1_out, B4, B2);
  or or_1 (out_5, xnor_1_out, B3, B1);
endmodule

module decodificadorB (
  input  B4,
  input  B3,
  input  B2,
  input  B1,
  output out_5
);

  wire not_1_out, xnor_1_out;

  xnor xnor_1 (xnor_1_out, B4, B3);
  not not_1 (not_1_out, B2);
  or or_1 (out_5, xnor_1_out, not_1_out);
endmodule

module decodificadorC (
  input  B4,
  input  B3,
  input  B2,
  input  B1,
  output out_5
);

  wire not_1_out;

  not not_1 (not_1_out, B3);
  or or_1 (out_5, B4, not_1_out, B2);
endmodule

module decodificadorD (
  input  B4,
  input  B3,
  input  B2,
  input  B1,
  output out_5
);

  wire and_1_out, and_2_out, and_3_out, and_4_out, not_1_out, not_2_out, not_3_out;

  not not_1 (not_1_out, B4);
  and and_1 (and_1_out, not_1_out, B3);
  not not_2 (not_2_out, B2);
  not not_3 (not_3_out, B3);
  and and_2 (and_2_out, not_1_out, not_2_out);
  and and_3 (and_3_out, not_2_out, B3);
  and and_4 (and_4_out, B2, not_3_out, B4);
  or or_1 (out_5, and_1_out, B1, and_2_out, and_3_out, and_4_out);
endmodule

module decodificadorE (
  input  B4,
  input  B3,
  input  B2,
  input  B1,
  output out_5
);

  wire and_1_out, and_2_out, not_1_out, not_2_out;

  not not_1 (not_1_out, B4);
  not not_2 (not_2_out, B2);
  and and_1 (and_1_out, not_1_out, not_2_out);
  and and_2 (and_2_out, not_1_out, B3);
  or or_1 (out_5, and_1_out, and_2_out);
endmodule

module decodificadorF (
  input  B4,
  input  B3,
  input  B2,
  input  B1,
  output out_5
);

  wire and_1_out, and_2_out, and_3_out, not_1_out, not_2_out;

  not not_1 (not_1_out, B4);
  not not_2 (not_2_out, B3);
  and and_1 (and_1_out, not_1_out, B2);
  and and_2 (and_2_out, not_1_out, not_2_out);
  and and_3 (and_3_out, B2, not_2_out);
  or or_1 (out_5, and_1_out, and_2_out, and_3_out, B1);
endmodule

module decodificadorG (
  input  B4,
  input  B3,
  input  B2,
  input  B1,
  output out_5
);

  wire and_1_out, not_1_out, xor_1_out;

  not not_1 (not_1_out, B4);
  xor xor_1 (xor_1_out, B3, B2);
  and and_1 (and_1_out, B2, not_1_out);
  or or_1 (out_5, and_1_out, xor_1_out, B1);
endmodule

module decodificadorBCD (
  input  D,
  input  C,
  input  B,
  input  A,
  output A_2,
  output B_2,
  output C_2,
  output D_2,
  output E,
  output F,
  output G
);

  decodificadorA decodificadora_1 (.B4(D), .B3(C), .B2(B), .B1(A), .out_5(A_2));
  decodificadorB decodificadorb_1 (.B4(D), .B3(C), .B2(B), .B1(A), .out_5(B_2));
  decodificadorC decodificadorc_1 (.B4(D), .B3(C), .B2(B), .B1(A), .out_5(C_2));
  decodificadorD decodificadord_1 (.B4(D), .B3(C), .B2(B), .B1(A), .out_5(D_2));
  decodificadorE decodificadore_1 (.B4(D), .B3(C), .B2(B), .B1(A), .out_5(E));
  decodificadorF decodificadorf_1 (.B4(D), .B3(C), .B2(B), .B1(A), .out_5(F));
  decodificadorG decodificadorg_1 (.B4(D), .B3(C), .B2(B), .B1(A), .out_5(G));
endmodule

module mod10 (
  input  EN,
  input  UP
);

  wire and_5_out, and_6_out, and_7_out, and_8_out, clock_1_out, clrA, clrB, CO, FFU0_q, FFU1_q, FFU2_q,
       FFU3_q, keepA, keepB, nUP, tog1, tog2, tog3, wdn, wup, xor_1_out, xor_2_out, xor_3_out, xor_4_out,
       xor_5_out, xor_6_out, xor_7_out, zero;

  not not_1 (nUP, UP);
  not not_2 (keepA, clrA);
  xor xor_1 (xor_1_out, FFU0_q, nUP);
  xor xor_2 (xor_2_out, FFU1_q, nUP);
  xor xor_3 (xor_3_out, FFU2_q, nUP);
  nor nor_1 (zero, FFU0_q, FFU1_q, FFU2_q, FFU3_q);
  and and_1 (wup, UP, FFU3_q, FFU0_q);
  and and_2 (wdn, zero, nUP);
  or or_1 (CO, wup, wdn);
  and and_3 (clrA, EN, wup);
  and and_4 (clrB, EN, wdn);
  nor nor_2 (keepB, clrA, clrB);
  and and_5 (and_5_out, keepA, xor_4_out);
  xor xor_4 (xor_4_out, tog3, FFU3_q);
  and and_6 (and_6_out, keepB, xor_5_out);
  xor xor_5 (xor_5_out, tog2, FFU2_q);
  and and_7 (and_7_out, keepB, xor_6_out);
  xor xor_6 (xor_6_out, tog1, FFU1_q);
  and and_8 (and_8_out, keepA, xor_7_out);
  xor xor_7 (xor_7_out, FFU0_q, EN);
  Clock clock_1 (.out(clock_1_out));
  and and_9 (tog1, xor_1_out, EN);
  and and_10 (tog2, xor_2_out, tog1);
  and and_11 (tog3, xor_3_out, tog2);
  D_Flip_Flop FFU3 (.clk(clock_1_out), .D(and_5_out), .Q(FFU3_q));  // open: Qn, preset, en, reset
  D_Flip_Flop FFU2 (.clk(clock_1_out), .D(and_6_out), .Q(FFU2_q));  // open: Qn, preset, en, reset
  D_Flip_Flop FFU1 (.clk(clock_1_out), .D(and_7_out), .Q(FFU1_q));  // open: Qn, preset, en, reset
  D_Flip_Flop FFU0 (.clk(clock_1_out), .D(and_8_out), .Q(FFU0_q));  // open: Qn, preset, en, reset
endmodule

module mod6 (
  input  EN,
  input  UP
);

  wire and_5_out, and_6_out, and_7_out, clock_1_out, clrA, clrB, CO, FFU1_q, FFU2_q, FFU3_q, keepA, keepB,
       nUP, tog1, tog2, wdn, wup, xor_1_out, xor_2_out, xor_3_out, xor_4_out, xor_5_out, zero;

  not not_1 (nUP, UP);
  not not_2 (keepA, clrA);
  xor xor_1 (xor_1_out, FFU1_q, nUP);
  xor xor_2 (xor_2_out, FFU2_q, nUP);
  nor nor_1 (zero, FFU1_q, FFU2_q, FFU3_q);
  and and_1 (wup, UP, FFU1_q, FFU3_q);
  and and_2 (wdn, zero, nUP);
  or or_1 (CO, wup, wdn);
  and and_3 (clrA, EN, wup);
  and and_4 (clrB, EN, wdn);
  nor nor_2 (keepB, clrA, clrB);
  and and_5 (and_5_out, keepA, xor_3_out);
  xor xor_3 (xor_3_out, tog2, FFU3_q);
  and and_6 (and_6_out, keepB, xor_4_out);
  xor xor_4 (xor_4_out, tog1, FFU2_q);
  and and_7 (and_7_out, keepA, xor_5_out);
  xor xor_5 (xor_5_out, EN, FFU1_q);
  Clock clock_1 (.out(clock_1_out));
  and and_8 (tog1, xor_1_out, EN);
  and and_9 (tog2, xor_2_out, tog1);
  D_Flip_Flop FFU3 (.clk(clock_1_out), .D(and_5_out), .Q(FFU3_q));  // open: Qn, preset, en, reset
  D_Flip_Flop FFU2 (.clk(clock_1_out), .D(and_6_out), .Q(FFU2_q));  // open: Qn, preset, en, reset
  D_Flip_Flop FFU1 (.clk(clock_1_out), .D(and_7_out), .Q(FFU1_q));  // open: Qn, preset, en, reset
endmodule

module contadorDeHoras (
  input  EN,
  input  UP,
  input  U0,
  input  U1,
  input  U2,
  input  U3,
  input  T0,
  input  T1
);

  wire last, nine, nUP, tog1, tog2, tog3, xor_1_out, xor_2_out, xor_3_out, zero;

  not not_1 (nUP, UP);
  xor xor_1 (xor_1_out, U0, nUP);
  xor xor_2 (xor_2_out, U1, nUP);
  xor xor_3 (xor_3_out, U2, nUP);
  nor nor_1 (zero, U0, U1, U2, U3);
  and and_1 (nine, U0, U3);
  and and_2 (last, U0, U1, T1);
  and and_3 (tog1, xor_1_out, EN);
  and and_4 (tog2, xor_2_out, tog1);
  and and_5 (tog3, xor_3_out, tog2);
endmodule
