// Logisim project projetoQuase_1.circ as structural Verilog: 13 circuits, main circuit main
module main (
  input  pinUP,
  input  pinEN
);

  wire Adm, Ads, AH, Ah_t, Aum, Aus, Bdm, Bds, BH, Bh_t, BTN, Bum, Bus, Cdm, Cds, CH, Ch_t, CLK, CO_MD,
       CO_MU, CO_SD, CO_SU, contadordehoras_1_t0, contadordehoras_1_t1, contadordehoras_1_u0,
       contadordehoras_1_u1, contadordehoras_1_u2, contadordehoras_1_u3, Cum, Cus, Ddm, Dds,
       decodificadorbcd_1_a_2, decodificadorbcd_1_b_2, decodificadorbcd_1_c_2, decodificadorbcd_1_d_2,
       decodificadorbcd_1_e, decodificadorbcd_1_f, decodificadorbcd_1_g, decodificadorbcd_2_a_2,
       decodificadorbcd_2_b_2, decodificadorbcd_2_c_2, decodificadorbcd_2_d_2, decodificadorbcd_2_e,
       decodificadorbcd_2_f, decodificadorbcd_2_g, decodificadorbcd_3_a_2, decodificadorbcd_3_b_2,
       decodificadorbcd_3_c_2, decodificadorbcd_3_d_2, decodificadorbcd_3_e, decodificadorbcd_3_f,
       decodificadorbcd_3_g, decodificadorbcd_4_a_2, decodificadorbcd_4_b_2, decodificadorbcd_4_c_2,
       decodificadorbcd_4_d_2, decodificadorbcd_4_e, decodificadorbcd_4_f, decodificadorbcd_4_g,
       decodificadorbcd_5_a_2, decodificadorbcd_5_b_2, decodificadorbcd_5_c_2, decodificadorbcd_5_d_2,
       decodificadorbcd_5_e, decodificadorbcd_5_f, decodificadorbcd_5_g, decodificadorbcd_6_a_2,
       decodificadorbcd_6_b_2, decodificadorbcd_6_c_2, decodificadorbcd_6_d_2, decodificadorbcd_6_e,
       decodificadorbcd_6_f, decodificadorbcd_6_g, DH, Dh_t, Dum, Dus, Edm, Eds, EH, Eh_t, EN_H, EN_MD,
       EN_MU, EN_SD, esp, Eum, Eus, Fdm, Fds, FH, Fh_t, Fum, Fus, Gdm, Gds, GH, Gh_t, Gum, Gus, mod6_1_q0,
       mod6_1_q1, mod6_1_q2, mod6_2_q0, mod6_2_q1, mod6_2_q2, mod10_1_q0, mod10_1_q1, mod10_1_q2, mod10_1_q3,
       mod10_2_q0, mod10_2_q1, mod10_2_q2, mod10_2_q3;

  and and_1 (EN_SD, pinEN, CO_SU);
  and and_2 (EN_MU, pinEN, CO_SU, CO_SD);
  and and_3 (EN_MD, EN_MU, CO_MU);
  and and_4 (EN_H, EN_MU, CO_MU, CO_MD);
  and and_5 (GH, esp, decodificadorbcd_1_g);
  and and_6 (FH, esp, decodificadorbcd_1_f);
  and and_7 (EH, esp, decodificadorbcd_1_e);
  and and_8 (DH, esp, decodificadorbcd_1_d_2);
  and and_9 (CH, esp, decodificadorbcd_1_c_2);
  and and_10 (BH, esp, decodificadorbcd_1_b_2);
  and and_11 (AH, decodificadorbcd_1_a_2, esp);
  contadorDeHoras contadordehoras_1 (
    .EN(EN_H), .UP(pinUP), .CLK(CLK), .T1(contadordehoras_1_t1), .T0(contadordehoras_1_t0),
    .U3(contadordehoras_1_u3), .U2(contadordehoras_1_u2), .U1(contadordehoras_1_u1), .U0(contadordehoras_1_u0));
  mod6 mod6_1 (.EN(EN_MD), .UP(pinUP), .CLK(CLK), .CO(CO_MD), .Q2(mod6_1_q2), .Q1(mod6_1_q1), .Q0(mod6_1_q0));
  mod10 mod10_1 (
    .EN(EN_MU), .UP(pinUP), .CLK(CLK), .CO(CO_MU), .Q3(mod10_1_q3), .Q2(mod10_1_q2), .Q1(mod10_1_q1),
    .Q0(mod10_1_q0));
  mod6 mod6_2 (.EN(EN_SD), .UP(pinUP), .CLK(CLK), .CO(CO_SD), .Q2(mod6_2_q2), .Q1(mod6_2_q1), .Q0(mod6_2_q0));
  mod10 mod10_2 (
    .EN(pinEN), .UP(pinUP), .CLK(CLK), .CO(CO_SU), .Q3(mod10_2_q3), .Q2(mod10_2_q2), .Q1(mod10_2_q1),
    .Q0(mod10_2_q0));
  decodificadorBCD decodificadorbcd_1 (
    .D(1'b0), .C(1'b0), .B(contadordehoras_1_t1), .A(contadordehoras_1_t0), .A_2(decodificadorbcd_1_a_2),
    .B_2(decodificadorbcd_1_b_2), .C_2(decodificadorbcd_1_c_2), .D_2(decodificadorbcd_1_d_2),
    .E(decodificadorbcd_1_e), .F(decodificadorbcd_1_f), .G(decodificadorbcd_1_g));
  and and_12 (Gh_t, esp, decodificadorbcd_2_g);
  and and_13 (Fh_t, esp, decodificadorbcd_2_f);
  and and_14 (Eh_t, esp, decodificadorbcd_2_e);
  and and_15 (Dh_t, esp, decodificadorbcd_2_d_2);
  and and_16 (Ch_t, esp, decodificadorbcd_2_c_2);
  and and_17 (Bh_t, esp, decodificadorbcd_2_b_2);
  and and_18 (Ah_t, esp, decodificadorbcd_2_a_2);
  decodificadorBCD decodificadorbcd_2 (
    .D(contadordehoras_1_u3), .C(contadordehoras_1_u2), .B(contadordehoras_1_u1), .A(contadordehoras_1_u0),
    .A_2(decodificadorbcd_2_a_2), .B_2(decodificadorbcd_2_b_2), .C_2(decodificadorbcd_2_c_2),
    .D_2(decodificadorbcd_2_d_2), .E(decodificadorbcd_2_e), .F(decodificadorbcd_2_f), .G(decodificadorbcd_2_g));
  controleDisplay controledisplay_1 (.EN(pinEN), .Cu(CO_SD), .Cd(CO_SU), .BTN(BTN), .CLK(CLK), .ENDISP(esp));
  and and_19 (Gdm, esp, decodificadorbcd_3_g);
  and and_20 (Fdm, esp, decodificadorbcd_3_f);
  and and_21 (Edm, esp, decodificadorbcd_3_e);
  and and_22 (Ddm, esp, decodificadorbcd_3_d_2);
  and and_23 (Cdm, esp, decodificadorbcd_3_c_2);
  and and_24 (Bdm, esp, decodificadorbcd_3_b_2);
  and and_25 (Adm, decodificadorbcd_3_a_2, esp);
  _7_Segment_Display u_7_segment_display_1 (.g(GH), .f(FH), .a(AH), .b(BH), .e(EH), .d(DH), .c(CH));  // open: dp
  decodificadorBCD decodificadorbcd_3 (
    .D(1'b0), .C(mod6_1_q2), .B(mod6_1_q1), .A(mod6_1_q0), .A_2(decodificadorbcd_3_a_2),
    .B_2(decodificadorbcd_3_b_2), .C_2(decodificadorbcd_3_c_2), .D_2(decodificadorbcd_3_d_2),
    .E(decodificadorbcd_3_e), .F(decodificadorbcd_3_f), .G(decodificadorbcd_3_g));
  _7_Segment_Display u_7_segment_display_2 (
    .g(Gh_t), .f(Fh_t), .a(Ah_t), .b(Bh_t), .e(Eh_t), .d(Dh_t), .c(Ch_t));  // open: dp
  and and_26 (Gum, esp, decodificadorbcd_4_g);
  and and_27 (Fum, esp, decodificadorbcd_4_f);
  and and_28 (Eum, esp, decodificadorbcd_4_e);
  and and_29 (Dum, esp, decodificadorbcd_4_d_2);
  and and_30 (Cum, esp, decodificadorbcd_4_c_2);
  and and_31 (Bum, esp, decodificadorbcd_4_b_2);
  and and_32 (Aum, decodificadorbcd_4_a_2, esp);
  decodificadorBCD decodificadorbcd_4 (
    .D(mod10_1_q3), .C(mod10_1_q2), .B(mod10_1_q1), .A(mod10_1_q0), .A_2(decodificadorbcd_4_a_2),
    .B_2(decodificadorbcd_4_b_2), .C_2(decodificadorbcd_4_c_2), .D_2(decodificadorbcd_4_d_2),
    .E(decodificadorbcd_4_e), .F(decodificadorbcd_4_f), .G(decodificadorbcd_4_g));
  _7_Segment_Display u_7_segment_display_3 (.g(Gdm), .f(Fdm), .a(Adm), .b(Bdm), .e(Edm), .d(Ddm), .c(Cdm));  // open: dp
  _7_Segment_Display u_7_segment_display_4 (.g(Gum), .f(Fum), .a(Aum), .b(Bum), .e(Eum), .d(Dum), .c(Cum));  // open: dp
  and and_33 (Gds, esp, decodificadorbcd_5_g);
  and and_34 (Fds, esp, decodificadorbcd_5_f);
  and and_35 (Eds, esp, decodificadorbcd_5_e);
  and and_36 (Dds, esp, decodificadorbcd_5_d_2);
  and and_37 (Cds, esp, decodificadorbcd_5_c_2);
  and and_38 (Bds, esp, decodificadorbcd_5_b_2);
  and and_39 (Ads, decodificadorbcd_5_a_2, esp);
  decodificadorBCD decodificadorbcd_5 (
    .D(1'b0), .C(mod6_2_q2), .B(mod6_2_q1), .A(mod6_2_q0), .A_2(decodificadorbcd_5_a_2),
    .B_2(decodificadorbcd_5_b_2), .C_2(decodificadorbcd_5_c_2), .D_2(decodificadorbcd_5_d_2),
    .E(decodificadorbcd_5_e), .F(decodificadorbcd_5_f), .G(decodificadorbcd_5_g));
  _7_Segment_Display u_7_segment_display_5 (.g(Gds), .f(Fds), .a(Ads), .b(Bds), .e(Eds), .d(Dds), .c(Cds));  // open: dp
  Clock clock_1 (.out(CLK));
  Button button_1 (.out(BTN));
  _7_Segment_Display u_7_segment_display_6 (.g(Gus), .f(Fus), .a(Aus), .b(Bus), .e(Eus), .d(Dus), .c(Cus));  // open: dp
  and and_40 (Gus, esp, decodificadorbcd_6_g);
  and and_41 (Fus, esp, decodificadorbcd_6_f);
  and and_42 (Eus, esp, decodificadorbcd_6_e);
  and and_43 (Dus, esp, decodificadorbcd_6_d_2);
  and and_44 (Cus, esp, decodificadorbcd_6_c_2);
  and and_45 (Bus, esp, decodificadorbcd_6_b_2);
  and and_46 (Aus, decodificadorbcd_6_a_2, esp);
  decodificadorBCD decodificadorbcd_6 (
    .D(mod10_2_q3), .C(mod10_2_q2), .B(mod10_2_q1), .A(mod10_2_q0), .A_2(decodificadorbcd_6_a_2),
    .B_2(decodificadorbcd_6_b_2), .C_2(decodificadorbcd_6_c_2), .D_2(decodificadorbcd_6_d_2),
    .E(decodificadorbcd_6_e), .F(decodificadorbcd_6_f), .G(decodificadorbcd_6_g));

  // Other names for the same wires on the sheet: EN = pinEN; UP = pinUP

  // Notes on the sheet:
  //   pinEN: pull=up
  //   pinUP: pull=up
endmodule

module decodificadorA (
  input  B4,
  input  B3,
  input  B2,
  input  B1,
  output out_5
);

  wire or_1_out, xnor_1_out;

  or or_1 (or_1_out, B4, B2);
  xnor xnor_1 (xnor_1_out, B3, B1);
  or or_2 (out_5, or_1_out, xnor_1_out);
endmodule

module decodificadorB (
  input  B4,
  input  B3,
  input  B2,
  input  B1,
  output out_5
);

  wire not_1_out, xnor_1_out;

  not not_1 (not_1_out, B3);
  xnor xnor_1 (xnor_1_out, B2, B1);
  or or_1 (out_5, not_1_out, xnor_1_out);
endmodule

module decodificadorC (
  input  B4,
  input  B3,
  input  B2,
  input  B1,
  output out_5
);

  wire not_1_out;

  not not_1 (not_1_out, B2);
  or or_1 (out_5, B3, not_1_out, B1);
endmodule

module decodificadorD (
  input  B4,
  input  B3,
  input  B2,
  input  B1,
  output out_5
);

  wire and_1_out, and_2_out, and_3_out, and_4_out, not_1_out, not_2_out, not_3_out, not_4_out, not_5_out;

  not not_1 (not_1_out, B3);
  not not_2 (not_2_out, B1);
  not not_3 (not_3_out, B1);
  not not_4 (not_4_out, B2);
  not not_5 (not_5_out, B3);
  and and_1 (and_1_out, not_1_out, not_2_out);
  and and_2 (and_2_out, B2, not_3_out);
  and and_3 (and_3_out, B3, not_4_out, B1);
  and and_4 (and_4_out, B2, not_5_out);
  or or_1 (out_5, B4, and_1_out, and_2_out, and_3_out, and_4_out);
endmodule

module decodificadorE (
  input  B4,
  input  B3,
  input  B2,
  input  B1,
  output out_5
);

  wire and_1_out, and_2_out, not_1_out, not_2_out, not_3_out;

  not not_1 (not_1_out, B1);
  and and_1 (and_1_out, not_1_out, not_2_out);
  not not_2 (not_2_out, B3);
  and and_2 (and_2_out, B2, not_3_out);
  not not_3 (not_3_out, B1);
  or or_1 (out_5, and_1_out, and_2_out);
endmodule

module decodificadorF (
  input  B4,
  input  B3,
  input  B2,
  input  B1,
  output out_5
);

  wire and_1_out, and_2_out, and_3_out, not_1_out, not_2_out, not_3_out, not_4_out;

  not not_1 (not_1_out, B2);
  not not_2 (not_2_out, B1);
  not not_3 (not_3_out, B2);
  and and_1 (and_1_out, B3, not_4_out);
  not not_4 (not_4_out, B1);
  and and_2 (and_2_out, not_1_out, not_2_out);
  and and_3 (and_3_out, B3, not_3_out);
  or or_1 (out_5, B4, and_2_out, and_3_out, and_1_out);
endmodule

module decodificadorG (
  input  B4,
  input  B3,
  input  B2,
  input  B1,
  output out_5
);

  wire and_1_out, not_1_out, xor_1_out;

  not not_1 (not_1_out, B1);
  xor xor_1 (xor_1_out, B3, B2);
  and and_1 (and_1_out, B2, not_1_out);
  or or_1 (out_5, B4, xor_1_out, and_1_out);
endmodule

module decodificadorBCD (
  input  D,
  input  C,
  input  B,
  input  A,
  output A_2,
  output B_2,
  output C_2,
  output D_2,
  output E,
  output F,
  output G
);

  decodificadorA decodificadora_1 (.B4(D), .B3(C), .B2(B), .B1(A), .out_5(A_2));
  decodificadorB decodificadorb_1 (.B4(D), .B3(C), .B2(B), .B1(A), .out_5(B_2));
  decodificadorC decodificadorc_1 (.B4(D), .B3(C), .B2(B), .B1(A), .out_5(C_2));
  decodificadorD decodificadord_1 (.B4(D), .B3(C), .B2(B), .B1(A), .out_5(D_2));
  decodificadorE decodificadore_1 (.B4(D), .B3(C), .B2(B), .B1(A), .out_5(E));
  decodificadorF decodificadorf_1 (.B4(D), .B3(C), .B2(B), .B1(A), .out_5(F));
  decodificadorG decodificadorg_1 (.B4(D), .B3(C), .B2(B), .B1(A), .out_5(G));
endmodule

module mod10 (
  input  EN,
  input  UP,
  input  CLK,
  output CO,
  output Q3,
  output Q2,
  output Q1,
  output Q0
);

  wire and_5_out, and_6_out, and_7_out, and_8_out, clrA, clrB, keepA, keepB, nUP, tog1, tog2, tog3, wdn, wup,
       xor_1_out, xor_2_out, xor_3_out, xor_4_out, xor_5_out, xor_6_out, xor_7_out, zero;

  not not_1 (nUP, UP);
  not not_2 (keepA, clrA);
  xor xor_1 (xor_1_out, Q0, nUP);
  xor xor_2 (xor_2_out, Q1, nUP);
  xor xor_3 (xor_3_out, Q2, nUP);
  nor nor_1 (zero, Q0, Q1, Q2, Q3);
  and and_1 (wup, UP, Q3, Q0);
  and and_2 (wdn, zero, nUP);
  or or_1 (CO, wup, wdn);
  and and_3 (clrA, EN, wup);
  and and_4 (clrB, EN, wdn);
  nor nor_2 (keepB, clrA, clrB);
  and and_5 (and_5_out, keepA, xor_4_out);
  xor xor_4 (xor_4_out, tog3, Q3);
  and and_6 (and_6_out, keepB, xor_5_out);
  xor xor_5 (xor_5_out, tog2, Q2);
  and and_7 (and_7_out, keepB, xor_6_out);
  xor xor_6 (xor_6_out, tog1, Q1);
  and and_8 (and_8_out, keepA, xor_7_out);
  xor xor_7 (xor_7_out, Q0, EN);
  and and_9 (tog1, xor_1_out, EN);
  and and_10 (tog2, xor_2_out, tog1);
  and and_11 (tog3, xor_3_out, tog2);
  D_Flip_Flop FFU3 (.clk(CLK), .D(and_5_out), .Q(Q3));  // open: Qn, preset, en, reset
  D_Flip_Flop FFU2 (.clk(CLK), .D(and_6_out), .Q(Q2));  // open: Qn, preset, en, reset
  D_Flip_Flop FFU1 (.clk(CLK), .D(and_7_out), .Q(Q1));  // open: Qn, preset, en, reset
  D_Flip_Flop FFU0 (.clk(CLK), .D(and_8_out), .Q(Q0));  // open: Qn, preset, en, reset
endmodule

module mod6 (
  input  EN,
  input  UP,
  input  CLK,
  output CO,
  output Q2,
  output Q1,
  output Q0
);

  wire and_5_out, and_6_out, and_7_out, clrA, clrB, keepA, keepB, nUP, tog1, tog2, wdn, wup, xor_1_out,
       xor_2_out, xor_3_out, xor_4_out, xor_5_out, zero;

  not not_1 (nUP, UP);
  not not_2 (keepA, clrA);
  xor xor_1 (xor_1_out, Q0, nUP);
  xor xor_2 (xor_2_out, Q1, nUP);
  nor nor_1 (zero, Q0, Q0, Q1, Q2);
  and and_1 (wup, UP, Q0, Q2);
  and and_2 (wdn, zero, nUP);
  or or_1 (CO, wup, wdn);
  and and_3 (clrA, EN, wup);
  and and_4 (clrB, EN, wdn);
  nor nor_2 (keepB, clrA, clrB);
  and and_5 (and_5_out, keepA, xor_3_out);
  xor xor_3 (xor_3_out, tog2, Q2);
  and and_6 (and_6_out, keepB, xor_4_out);
  xor xor_4 (xor_4_out, tog1, Q1);
  and and_7 (and_7_out, keepA, xor_5_out);
  xor xor_5 (xor_5_out, EN, Q0);
  and and_8 (tog1, xor_1_out, EN);
  and and_9 (tog2, xor_2_out, tog1);
  D_Flip_Flop FFU3 (.clk(CLK), .D(and_5_out), .Q(Q2));  // open: Qn, preset, en, reset
  D_Flip_Flop FFU2 (.clk(CLK), .D(and_6_out), .Q(Q1));  // open: Qn, preset, en, reset
  D_Flip_Flop FFU1 (.clk(CLK), .D(and_7_out), .Q(Q0));  // open: Qn, preset, en, reset
endmodule

// horas
module contadorDeHoras (
  input  EN,
  input  UP,
  input  CLK,
  output T1,
  output T0,
  output U3,
  output U2,
  output U1,
  output U0
);

  wire and_5_out, and_7_out, and_8_out, and_9_out, and_14_out, and_15_out, and_16_out, and_17_out, cA, dnT,
       dw, dwN, keep0, keep1, keep2, keep3, last, nine, nm, not_4_out, nUP, nzT, p2, tog1, tog2, tog3, tT0,
       tT1, xor_1_out, xor_2_out, xor_3_out, xor_4_out, xor_5_out, xor_6_out, xor_7_out, xor_8_out,
       xor_9_out, zero, zT;

  not not_1 (nUP, UP);
  xor xor_1 (xor_1_out, U0, nUP);
  xor xor_2 (xor_2_out, U1, nUP);
  xor xor_3 (xor_3_out, U2, nUP);
  nor nor_1 (zero, U0, U1, U2, U3);
  and and_1 (nine, U0, U3);
  and and_2 (last, U0, U1, T1);
  or or_1 (nm, nine, last);
  and and_3 (cA, EN, UP, nm);
  and and_4 (dw, EN, nUP, zero);
  or or_2 (nzT, T0, T1);
  not not_2 (zT, nzT);
  and and_5 (and_5_out, zT, dw);
  and and_6 (dwN, dw, nzT);
  nor nor_2 (keep1, cA, dwN);
  nor nor_3 (keep2, cA, dw);
  not not_3 (keep0, cA);
  and and_7 (and_7_out, EN, UP, nine);
  and and_8 (and_8_out, nine, T0);
  not not_4 (not_4_out, T0);
  and and_9 (and_9_out, EN, UP, p2);
  xor xor_4 (xor_4_out, T1, tT1);
  xor xor_5 (xor_5_out, T0, tT0);
  xor xor_6 (xor_6_out, U3, tog3);
  xor xor_7 (xor_7_out, U2, tog2);
  xor xor_8 (xor_8_out, U1, tog1);
  xor xor_9 (xor_9_out, U0, EN);
  and and_10 (tog1, xor_1_out, EN);
  and and_11 (tog2, xor_2_out, tog1);
  and and_12 (tog3, xor_3_out, tog2);
  nor nor_4 (keep3, cA, and_5_out);
  or or_3 (tT0, dwN, and_7_out);
  or or_4 (p2, last, and_8_out);
  and and_13 (dnT, dw, not_4_out);
  or or_5 (tT1, dnT, and_9_out);
  and and_14 (and_14_out, keep3, xor_6_out);
  and and_15 (and_15_out, keep2, xor_7_out);
  and and_16 (and_16_out, keep1, xor_8_out);
  and and_17 (and_17_out, keep0, xor_9_out);
  D_Flip_Flop d_ff_1 (.clk(CLK), .D(xor_4_out), .Q(T1));  // open: Qn, preset, en, reset
  D_Flip_Flop d_ff_2 (.clk(CLK), .D(xor_5_out), .Q(T0));  // open: Qn, preset, en, reset
  D_Flip_Flop d_ff_3 (.clk(CLK), .D(and_14_out), .Q(U3));  // open: Qn, preset, en, reset
  D_Flip_Flop d_ff_4 (.clk(CLK), .D(and_15_out), .Q(U2));  // open: Qn, preset, en, reset
  D_Flip_Flop d_ff_5 (.clk(CLK), .D(and_16_out), .Q(U1));  // open: Qn, preset, en, reset
  D_Flip_Flop d_ff_6 (.clk(CLK), .D(and_17_out), .Q(U0));  // open: Qn, preset, en, reset
endmodule

// H
module controleDisplay (
  input  EN,
  input  Cu,
  input  Cd,
  input  BTN,
  input  CLK,
  output ENDISP
);

  wire and_6_out, and_7_out, and_8_out, and_9_out, d_ff_1_q, d_ff_2_q, d_ff_3_q, d_ff_5_q, d_ff_6_q, go,
       not_1_out, not_2_out, nTrig, or_2_out, press, tg1, tg2, trig, trigA, undriven, undriven_2, undriven_3,
       undriven_4, undriven_5, xor_1_out, xor_2_out, xor_3_out;

  not not_1 (not_1_out, d_ff_1_q);
  not not_2 (not_2_out, d_ff_5_q);
  not not_3 (nTrig, trig);
  and and_1 (go, not_1_out, ENDISP);
  and and_2 (press, not_2_out, d_ff_6_q);
  and and_3 (trigA, EN, Cu, Cd);
  or or_1 (trig, trigA, press);
  and and_4 (tg1, d_ff_3_q, go);
  and and_5 (tg2, d_ff_3_q, d_ff_2_q, go);
  xor xor_1 (xor_1_out, d_ff_1_q, tg2);
  xor xor_2 (xor_2_out, d_ff_2_q, tg1);
  xor xor_3 (xor_3_out, d_ff_3_q, go);
  or or_2 (or_2_out, trig, go);
  and and_6 (and_6_out, BTN, not_1_out);
  and and_7 (and_7_out, xor_1_out, nTrig);
  and and_8 (and_8_out, xor_2_out, nTrig);
  and and_9 (and_9_out, xor_3_out, nTrig);
  D_Flip_Flop d_ff_1 (.clk(CLK), .D(and_7_out), .Q(d_ff_1_q), .preset(undriven));  // open: Qn, en, reset
  D_Flip_Flop d_ff_2 (.clk(CLK), .D(and_8_out), .Q(d_ff_2_q), .preset(undriven_2));  // open: Qn, en, reset
  D_Flip_Flop d_ff_3 (.clk(CLK), .D(and_9_out), .Q(d_ff_3_q), .preset(undriven_3));  // open: Qn, en, reset
  D_Flip_Flop d_ff_4 (.clk(CLK), .D(or_2_out), .Q(ENDISP), .preset(undriven_4));  // open: Qn, en, reset
  D_Flip_Flop d_ff_5 (.clk(CLK), .D(d_ff_6_q), .Q(d_ff_5_q), .preset(undriven_5));  // open: Qn, en, reset
  D_Flip_Flop d_ff_6 (.clk(CLK), .D(BTN), .Q(d_ff_6_q), .preset(and_6_out));  // open: Qn, en, reset
endmodule
